# Fritzing sketch 3320LPF_Test1 (saved by Fritzing 0.9.4)
breadboards: 2

parts:
  R1 = Resistor [tolerance=±5% resistance=91k package=THT]
  R2 = Resistor [tolerance=±5% resistance=100k package=THT]
  R3 = Resistor [tolerance=±5% resistance=220k package=THT]
  R4 = Resistor [tolerance=±5% resistance=91k package=THT]
  R5 = Resistor [tolerance=±5% resistance=220k package=THT]
  R6 = Resistor [tolerance=±5% resistance=100k package=THT]
  C1 = Film/Foil Capacitor [capacitance=100nF voltage=35V package="5mm [THT, pp]"]
  R7 = Resistor [tolerance=±5% resistance=1.5k package=THT]
  R8 = Resistor [tolerance=±5% resistance=1.8k package=THT]
  C2 = Film/Foil Capacitor [capacitance=100nF voltage=35V package="5mm [THT, pp]"]
  R9 = Resistor [tolerance=±5% resistance=100k package=THT]
  C3 = Film/Foil Capacitor [capacitance=100nF voltage=35V package="5mm [THT, pp]"]
  R10 = Resistor [tolerance=±5% resistance=68k package=THT]
  R11 = Resistor [tolerance=±5% resistance=100k package=THT]
  C4 = Film/Foil Capacitor [capacitance=100nF voltage=35V package="5mm [THT, pp]"]
  C5 = Film/Foil Capacitor [capacitance=100nF voltage=35V package="5mm [THT, pp]"]
  R12 = Resistor [tolerance=±5% resistance=100k package=THT]
  R13 = Resistor [tolerance=±5% resistance=91k package=THT]
  R14 = Resistor [tolerance=±5% resistance=220k package=THT]
  R15 = Resistor [tolerance=±5% resistance=91k package=THT]
  R16 = Resistor [tolerance=±5% resistance=100k package=THT]
  U2 = mystery part, 18 pins [chip_label=V3320]
  C6 = Electrolytic Capacitor [capacitance=1µF package="100 mil [THT, electrolytic]"]
  C7 = Electrolytic Capacitor [capacitance=1µF package="100 mil [THT, electrolytic]"]
  C9 = Electrolytic Capacitor [capacitance=1µF package="100 mil [THT, electrolytic]"]
  IC1 = Dual Op-Amp [package=dip08]
  R17 = Resistor [tolerance=±5% resistance=220k package=THT]
  R18 = Resistor [tolerance=±5% resistance=100k package=THT]
  R19 = Resistor [tolerance=±5% resistance=51k package=THT]
  R20 = Resistor [tolerance=±5% resistance=3k package=THT]
  C10 = Ceramic Capacitor [capacitance=100nF package="100 mil [THT, multilayer]"]
  C11 = Ceramic Capacitor [capacitance=100nF package="100 mil [THT, multilayer]"]
  C12 = Electrolytic Capacitor [capacitance=1µF package="100 mil [THT, electrolytic]"]
  R21 = Resistor [tolerance=±5% resistance=1k package=THT]

nets:
  N1: R1.Pin_0, R16.Pin_1, U2.pin7
  N2: R1.Pin_1, R3.Pin_1, R6.Pin_0, U2.pin2
  N3: R2.Pin_0, R4.Pin_1, R5.Pin_1, U2.pin17
  N4: R2.Pin_1, R13.Pin_0, U2.pin15
  N5: R3.Pin_0, R5.Pin_0, R7.Pin_1, R14.Pin_0, C7.-, C9.-, C10.1
  N6: R4.Pin_0, R6.Pin_1, U2.pin6
  N7: C1.-, R8.Pin_0, C2.+, R10.Pin_0, C4.+, C5.-, U2.pin3, C6.-, C7.+, C9.+, IC1.A_V-, IC1.B_+IN, R18.Pin_0, R20.Pin_1, C10.0, C11.1, C12.-
  N8: C1.+, U2.pin16
  N9: R7.Pin_0, U2.pin13
  N10: R8.Pin_1, R9.Pin_0, U2.pin12
  N11: C2.-, U2.pin11
  N12: C3.-, R12.Pin_1, U2.pin10
  N13: C3.+, R10.Pin_1, IC1.A_+IN
  N14: R11.Pin_0, U2.pin9
  N15: C4.-, U2.pin4
  N16: C5.+, U2.pin5
  N17: R12.Pin_0, R13.Pin_1, R14.Pin_1, U2.pin18
  N18: R15.Pin_1, R16.Pin_0, U2.pin1
  N19: U2.pin8, R19.Pin_0, R20.Pin_0
  N20: U2.pin14, C6.+, IC1.A_V+, C11.0, C12.+
  N21: IC1.A_OUT, R17.Pin_0, R19.Pin_1, R21.Pin_1
  N22: IC1.A_-IN, R17.Pin_1, R18.Pin_1
  N23: IC1.B_-IN, IC1.B_OUT

notes:
  WAVOUT
  RES
  CV
  WAV
  IN
  -12V GND
  GND
  +12V
  -12V
  GND
  GND +12V
  FREQ
  CV
