# Fritzing sketch 3320LPF_Test2 (saved by Fritzing 0.9.4)
breadboards: 2

parts:
  R1 = Resistor [tolerance=±5% resistance=91k package=THT]
  R2 = Resistor [tolerance=±5% resistance=100k package=THT]
  R3 = Resistor [tolerance=±5% resistance=220k package=THT]
  R4 = Resistor [tolerance=±5% resistance=91k package=THT]
  R5 = Resistor [tolerance=±5% resistance=220k package=THT]
  R6 = Resistor [tolerance=±5% resistance=100k package=THT]
  C1 = Film/Foil Capacitor [capacitance=100nF voltage=35V package="5mm [THT, pp]"]
  R7 = Resistor [tolerance=±5% resistance=1.5k package=THT]
  C2 = Film/Foil Capacitor [capacitance=100nF voltage=35V package="5mm [THT, pp]"]
  C3 = Film/Foil Capacitor [capacitance=100nF voltage=35V package="5mm [THT, pp]"]
  R10 = Resistor [tolerance=±5% resistance=68k package=THT]
  C4 = Film/Foil Capacitor [capacitance=100nF voltage=35V package="5mm [THT, pp]"]
  C5 = Film/Foil Capacitor [capacitance=100nF voltage=35V package="5mm [THT, pp]"]
  R12 = Resistor [tolerance=±5% resistance=100k package=THT]
  R13 = Resistor [tolerance=±5% resistance=91k package=THT]
  R14 = Resistor [tolerance=±5% resistance=220k package=THT]
  R15 = Resistor [tolerance=±5% resistance=91k package=THT]
  R16 = Resistor [tolerance=±5% resistance=100k package=THT]
  U2 = mystery part, 18 pins [chip_label=V3320]
  C6 = Electrolytic Capacitor [capacitance=1µF package="100 mil [THT, electrolytic]"]
  C7 = Electrolytic Capacitor [capacitance=1µF package="100 mil [THT, electrolytic]"]
  C9 = Electrolytic Capacitor [capacitance=1µF package="100 mil [THT, electrolytic]"]
  IC1 = Dual Op-Amp [package=dip08]
  R17 = Resistor [tolerance=±5% resistance=220k package=THT]
  R18 = Resistor [tolerance=±5% resistance=100k package=THT]
  R19 = Resistor [tolerance=±5% resistance=51k package=THT]
  R20 = Resistor [tolerance=±5% resistance=3k package=THT]
  C10 = Ceramic Capacitor [capacitance=100nF package="100 mil [THT, multilayer]"]
  C11 = Ceramic Capacitor [capacitance=100nF package="100 mil [THT, multilayer]"]
  C12 = Electrolytic Capacitor [capacitance=1µF package="100 mil [THT, electrolytic]"]
  R21 = Resistor [tolerance=±5% resistance=1k package=THT]
  R22 = Resistor [tolerance=±5% resistance=82k package=THT]
  R23 = Resistor [tolerance=±5% resistance=220k package=THT]
  R24 = Rotary Potentiometer (Small) [maximum_resistance=100kΩ package=THT]
  R25 = Rotary Potentiometer (Small) [maximum_resistance=100kΩ package=THT]
  IC2 = Dual Op-Amp [package=dip08]
  C13 = Ceramic Capacitor [capacitance=100nF package="100 mil [THT, multilayer]"]
  C14 = Ceramic Capacitor [capacitance=100nF package="100 mil [THT, multilayer]"]
  R26 = Resistor [tolerance=±5% resistance=2k package=THT]
  R27 = Resistor [tolerance=±5% resistance=51k package=THT]
  R28 = Rotary Potentiometer (Small) [maximum_resistance=100kΩ package=THT]
  R29 = Resistor [tolerance=±5% resistance=150k package=THT]
  R30 = Rotary Potentiometer (Small) [maximum_resistance=100kΩ package=THT]
  R31 = Resistor [tolerance=±5% resistance=100k package=THT]
  R32 = TRIMPOT [package=trimpot_pth_s3_lock]
  R33 = Rotary Potentiometer (Small) [maximum_resistance=100kΩ package=THT]

nets:
  N1: R1.Pin_0, R16.Pin_1, U2.pin7
  N2: R1.Pin_1, R3.Pin_1, R6.Pin_0, U2.pin2
  N3: R2.Pin_0, R4.Pin_1, R5.Pin_1, U2.pin17
  N4: R2.Pin_1, R13.Pin_0, U2.pin15
  N5: R3.Pin_0, R5.Pin_0, R7.Pin_1, R14.Pin_0, C7.-, C9.-, C10.1, IC2.A_V-, C13.1, R32.CCW
  N6: R4.Pin_0, R6.Pin_1, U2.pin6
  N7: C1.-, C2.+, R10.Pin_0, C4.+, C5.-, U2.pin3, C6.-, C7.+, C9.+, IC1.A_V-, IC1.B_+IN, R18.Pin_0, R20.Pin_1, C10.0, C11.1, C12.-, R24.leg1, R25.leg1, IC2.A_+IN, IC2.B_+IN, C13.0, C14.1, R28.leg1, R30.leg1, R33.leg1
  N8: C1.+, U2.pin16
  N9: R7.Pin_0, U2.pin13
  N10: C2.-, U2.pin11
  N11: C3.-, R12.Pin_1, U2.pin10
  N12: C3.+, R10.Pin_1, IC1.A_+IN
  N13: C4.-, U2.pin4
  N14: C5.+, U2.pin5
  N15: R12.Pin_0, R13.Pin_1, R14.Pin_1, U2.pin18
  N16: R15.Pin_0, R33.wiper
  N17: R15.Pin_1, R16.Pin_0, U2.pin1
  N18: U2.pin8, R19.Pin_0, R20.Pin_0
  N19: U2.pin9, R22.Pin_0, R23.Pin_0
  N20: U2.pin12, IC2.A_OUT, R26.Pin_0
  N21: U2.pin14, C6.+, IC1.A_V+, C11.0, C12.+, R24.leg2, IC2.A_V+, C14.0, R30.leg2
  N22: IC1.A_OUT, R17.Pin_0, R19.Pin_1, R21.Pin_1
  N23: IC1.A_-IN, R17.Pin_1, R18.Pin_1
  N24: IC1.B_-IN, IC1.B_OUT
  N25: R22.Pin_1, R25.wiper
  N26: R23.Pin_1, R24.wiper
  N27: IC2.A_-IN, R26.Pin_1, R27.Pin_0, R29.Pin_0, R31.Pin_0
  N28: IC2.B_-IN, IC2.B_OUT
  N29: R27.Pin_1, R28.wiper
  N30: R29.Pin_1, R30.wiper
  N31: R31.Pin_1, R32.WIPER, R32.CW

notes:
  WAVOUT
  RES_CV
  100k/B
  WAV_IN
  50k/A
  -12V GND
  GND
  +12V
  -12V
  GND
  GND +12V
  FREQ_CV
  100k/B
  Resonance
  100k/B
  Cutoff
  100k/B
  Cutoff
  Trim 100k
